# Fritzing sketch Arduino-Domoticz-Gateway (saved by Fritzing 0.9.1b)
breadboards: 1

parts:
  Part2 = Arduino Ethernet Shield (Rev3)
  U1 = RF-LINK_RX [package=rf-link_rx]
  ANT1 = Antenna
  part = Antenna  # not connected
  U2 = Mystery Part - 3 pins [chip_label=DS18B20 package=THT]
  R1 = Resistor [tolerance=±5% resistance=4.7k package=THT]

nets:
  5V: Part2.5V, U1.+5V, R1.Pin_1
  GND: Part2.GND, U1.GND, U2.pin1, U2.pin3
  N1: Part2.D2, U1.DATA
  N2: Part2.D7, U2.pin2, R1.Pin_0
  N3: U1.ANT, ANT1.antenna_lead

custom parts:
  Mystery Part - 3 pins: A dummy, proxy, ersatz, stand-in part for whatever you want. With 3 pins on a 100 mil inline pin header footprint.
